# Fritzing sketch circuito_base01 (saved by Fritzing 0.9.2b)

parts:
  ESP8266-1 = ESP8266-12 [part_number=ESP8266-12]
  R1 = Resistor [tolerance=±5% resistance=10k package=THT]
  R2 = Resistor [tolerance=±5% resistance=10k package=THT]
  R3 = Resistor [tolerance=±5% resistance=10k package=THT]
  R4 = Resistor [tolerance=±5% resistance=10k package=THT]
  USBUART1 = PL2303 USB UART Breakout
  IC1 = V_REG_LD1117VXX [package=78xxl]
  C1 = Ceramic Capacitor [capacitance=100nF package="100 mil [THT, multilayer]"]
  C2 = Ceramic Capacitor [capacitance=100nF package="100 mil [THT, multilayer]"]
  C3 = Capacitor Polarized [package=cpol-radial-10uf-25v]

nets:
  N1: ESP8266-1.REST, R2.Pin_1
  N2: ESP8266-1.CH_PD, R3.Pin_1
  N3: ESP8266-1.VCC, R2.Pin_0, R3.Pin_0, R4.Pin_1, IC1.OUT, C2.1, C3.-
  N4: ESP8266-1.TXD, USBUART1.RXD
  N5: ESP8266-1.RXD, USBUART1.TXD
  N6: ESP8266-1.GPIO0, R4.Pin_0
  N7: ESP8266-1.GPIO15, R1.Pin_0
  GND: ESP8266-1.GND, R1.Pin_1, USBUART1.GND, IC1.GND, C1.1, C2.0, C3.+
  N8: USBUART1.VCCIO, IC1.IN, C1.0

notes:
  mettere a GND per programmare

custom parts:
  PL2303 USB UART Breakout: PL2302 Usb Uart Breakout Board with Battery
